// Digital circuit lab04.dig as structural Verilog
module lab04 (
  input  clk,
  input  rst,
  output [31:0] PC,
  output [5:0] opcode,
  output [4:0] src1__addr,
  output [31:0] src1__out,
  output [4:0] src2__addr,
  output [31:0] src2__out,
  output [4:0] dst__addr,
  output [31:0] dst__data
);

  wire and_1_out, u_alu_3_zero, u_control_unit_alu_src, u_control_unit_branch, u_control_unit_mem_read,
       u_control_unit_mem_to_reg, u_control_unit_mem_write, u_control_unit_reg_dst, u_control_unit_reg_write;
  wire [1:0] u_control_unit_alu_op;
  wire [3:0] u_alu_control_alu_control;
  wire [15:0] cpumemory_d2;
  wire [31:0] barrelshifter_1_out, bitextender_1_out, cpumemory_d1, multiplexer_1_out, multiplexer_3_out,
       u_alu_2_result, u_alu_3_result, u_alu_result;

  BarrelShifter #(.Bits(32)) barrelshifter_1 (.in(bitextender_1_out), .shift(6'b000010), .out(barrelshifter_1_out));
  gen_register #(.applicationType("IVERILOG"), .CodeFile("./gen_register.v")) u_gen_register (
    .clk(clk), .rst(rst), .write_en(clk), .data_in(multiplexer_1_out), .data_out(PC));
  alu #(.applicationType("IVERILOG"), .CodeFile("./alu.v")) u_alu (
    .alu_control(4'b0010), .A(PC), .B(32'h4), .result(u_alu_result));  // open: zero
  RAMDualAccess #(.AddrBits(8), .isProgramMemory("true"), .Bits(32)) cpumemory (
    .str(u_control_unit_mem_write), .C(clk), .ld(u_control_unit_mem_read), .A1(u_alu_3_result[7:0]),
    .Din1(src2__out), .A2(PC[7:0]), .D1(cpumemory_d1), .D2({opcode, src1__addr, src2__addr, cpumemory_d2}));
  alu #(.applicationType("IVERILOG"), .CodeFile("./alu.v")) u_alu_2 (
    .alu_control(4'b0010), .A(u_alu_result), .B(barrelshifter_1_out), .result(u_alu_2_result));  // open: zero
  and and_1 (and_1_out, u_control_unit_branch, u_alu_3_zero);
  BitExtender #(.inputBits(16), .outputBits(32)) bitextender_1 (.in(cpumemory_d2), .out(bitextender_1_out));
  Multiplexer #(.Bits(32)) multiplexer_1 (
    .sel(and_1_out), .in_0(u_alu_result), .in_1(u_alu_2_result), .out(multiplexer_1_out));
  Multiplexer #(.Bits(5)) multiplexer_2 (
    .sel(u_control_unit_reg_dst), .in_0(src2__addr), .in_1(cpumemory_d2[15:11]), .out(dst__addr));
  control_unit #(.applicationType("IVERILOG"), .CodeFile("./control_unit.v")) u_control_unit (
    .instr_op(opcode), .reg_dst(u_control_unit_reg_dst), .branch(u_control_unit_branch),
    .mem_read(u_control_unit_mem_read), .mem_to_reg(u_control_unit_mem_to_reg),
    .alu_op(u_control_unit_alu_op), .mem_write(u_control_unit_mem_write), .alu_src(u_control_unit_alu_src),
    .reg_write(u_control_unit_reg_write));
  cpu_registers #(.applicationType("IVERILOG"), .CodeFile("./cpu_registers.v")) u_cpu_registers (
    .clk(clk), .rst(rst), .write_en(u_control_unit_reg_write), .src1_addr(src1__addr),
    .src2_addr(src2__addr), .dst_addr(dst__addr), .data_in(dst__data), .src1_out(src1__out),
    .src2_out(src2__out));
  alu_control #(.applicationType("IVERILOG"), .CodeFile("./alu_control.v")) u_alu_control (
    .alu_op(u_control_unit_alu_op), .funct(cpumemory_d2[5:0]), .alu_control(u_alu_control_alu_control));
  Multiplexer #(.Bits(32)) multiplexer_3 (
    .sel(u_control_unit_alu_src), .in_0(src2__out), .in_1(bitextender_1_out), .out(multiplexer_3_out));
  alu #(.applicationType("IVERILOG"), .CodeFile("./alu.v")) u_alu_3 (
    .alu_control(u_alu_control_alu_control), .A(src1__out), .B(multiplexer_3_out), .zero(u_alu_3_zero),
    .result(u_alu_3_result));
  Multiplexer #(.Bits(32)) multiplexer_4 (
    .sel(u_control_unit_mem_to_reg), .in_0(u_alu_3_result), .in_1(cpumemory_d1), .out(dst__data));

  // Notes on the sheet:
  //   Inputs
  //   PC
  //   Outputs for testing
endmodule
